# Fritzing sketch Morse Code Decoder Responds to Words (saved by Fritzing 0.9.3b)
breadboards: 1

parts:
  Part1 = Arduino Uno (Rev3)
  M1 = Dagu DGServo 9g (Pan and tilt) [part_number=RS001B]
  S1 = Momentary Switch [package=ksa_sealed_tac_switch]
  R1 = Resistor [tolerance=±5% resistance=10k package="0805 [SMD]"]
  LED1 = LED - 5mm [color="White (8000K)" package="5 mm [THT]"]
  J1 = Piezo Speaker
  IC2 = L293D [package=THT]
  M2 = DC Motor
  M3 = DC Motor

nets:
  N1: Part1.A4/SDA, LED1.anode
  N2: Part1.A5/SCL, J1.pin2
  N3: Part1.D8, IC2.In_4
  N4: Part1.D10_PWM/SS, S1.1
  N5: Part1.D13/SCK, M1.pulse
  N6: Part1.GND, J1.pin1
  N7: Part1.D2, IC2.In_1
  N8: Part1.D6_PWM, IC2.Enable_1
  N9: Part1.D7, IC2.Out_3_(_Controlled_by_Enable_2_), M2.pin_2
  N10: M1.gnd, LED1.cathode, IC2.0V
  N11: M1.vcc, R1.Pin_1, IC2.+V
  N12: S1.2, R1.Pin_0
  N13: IC2.Out_1_(_Controlled_by_Enable_1_), M3.pin_1
  N14: IC2.Out_2_(_Controlled_by_Enable_1_), M3.pin_2
  N15: IC2.Out_4_(_Controlled_by_Enable_2_), M2.pin_1
